# Fritzing sketch duo-button-01-external-pulldown (saved by Fritzing 0.9.3b)
breadboards: 1

parts:
  Part1 = RedBear Duo
  S1 = Pushbutton [package="[THT]"]
  R1 = Resistor [tolerance=±5% resistance=10k package=THT]

nets:
  N1: Part1.GND, R1.Pin_1
  N2: Part1.D0, S1.Pin_1, S1.Pin_2, R1.Pin_0
  N3: Part1.3V3, S1.Pin_3, S1.Pin_4

custom parts:
  RedBear Duo: Duo is a thumb-size development board made to simplify the building process of Internet of Things (IoT). This part is a modification of the Particle Photon part by Brett Walach,Fabian Althaus
