# Fritzing sketch duo-button-03-internal-pullup (saved by Fritzing 0.9.3b)
breadboards: 1

parts:
  Part1 = RedBear Duo
  S1 = Pushbutton [package="[THT]"]

nets:
  N1: Part1.GND, S1.Pin_1, S1.Pin_2
  N2: Part1.D0, S1.Pin_3, S1.Pin_4

custom parts:
  RedBear Duo: Duo is a thumb-size development board made to simplify the building process of Internet of Things (IoT). This part is a modification of the Particle Photon part by Brett Walach,Fabian Althaus
