# Fritzing sketch duo-button-04-internal-pulldown (saved by Fritzing 0.9.3b)
breadboards: 1

parts:
  S1 = Pushbutton [package="[THT]"]
  Part1 = RedBear-Duo

nets:
  N1: S1.Pin_1, S1.Pin_2, Part1.3V3
  N2: S1.Pin_3, S1.Pin_4, Part1.D0

custom parts:
  RedBear-Duo: Duo is a thumb-size development board made to simplify the building process of Internet of Things (IoT). This part is a modification of the Particle Photon part by Brett Walach,Fabian Althaus
