# Fritzing sketch duo-joystick (saved by Fritzing 0.9.3b)
breadboards: 1

parts:
  Part1 = RedBear-Duo
  Part2 = Adafruit Analog 2-Axis Joystick [part_number="Adafruit #512"]

nets:
  N1: Part1.A0, Part2.XOUT
  GND: Part1.GND, Part2.GND
  3V3: Part1.3V3, Part2.VCC

custom parts:
  RedBear-Duo: Duo is a thumb-size development board made to simplify the building process of Internet of Things (IoT). This part is a modification of the Particle Photon part by Brett Walach,Fabian Althaus
  Adafruit Analog 2-Axis Joystick: This mini-kit makes it easy to mount a PSP/Xbox-like thumb joystick to your project. The thumbstick is an analog joystick - more accurate and sensitive than just 'directional' joysticks - with a 'press in to select' button. Since it's analog, you'll need two analog reading pins on your microcontroller to determine X and Y. Having an extra digital input will let you read the switch. The pack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
