# Fritzing sketch duo-lis3dh (saved by Fritzing 0.9.3b)
breadboards: 1

parts:
  Part1 = RedBear-Duo
  Part2 = Adafruit LIS3DH [part_number="Adafruit #2809"]

nets:
  GND: Part1.GND, Part2.GND
  N1: Part1.D0, Part2.SDA
  N2: Part1.D1, Part2.SCL
  3V3: Part1.3V3, Part2.VIN
  N3: Part2.ADC2, Part2.ADC3

custom parts:
  RedBear-Duo: Duo is a thumb-size development board made to simplify the building process of Internet of Things (IoT). This part is a modification of the Particle Photon part by Brett Walach,Fabian Althaus
  Adafruit LIS3DH: The LIS3DH is a very popular low power triple-axis accelerometer. It's low-cost, but has just about every 'extra' you'd want in an accelerometer: Three axis sensing, 10-bit precision ±2g/±4g/±8g/±16g selectable scaling Both I2C (2 possible addresses) and SPI interface options Interrupt output Multiple data rate options 1 Hz to 5Khz As low as 2uA current draw (just the chip itself, not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
